// Logisim project SPI.circ as structural Verilog: 3 circuits, main circuit Master-reg
module Basic_SPI (
  input  in_1,
  input  [1:0] in_2
);

  wire Master_mosi, Master_sclk, multiplexer_1_out, Slave_1_miso, Slave_2_miso, Slave_3_miso;
  wire [2:0] Master_cs;

  Master_reg Master (
    .MISO(multiplexer_1_out), .Enable(in_1), .Slave_select(in_2), .SCLK(Master_sclk), .MOSI(Master_mosi),
    .CS(Master_cs));
  Multiplexer #(.select(2), .enable("false")) multiplexer_1 (
    .in0(Slave_1_miso), .in1(Slave_2_miso), .in2(Slave_3_miso), .in3(1'b0), .out(multiplexer_1_out),
    .sel(in_2));
  Slave_reg Slave_3 (.SCLK(Master_sclk), .MOSI(Master_mosi), .Enable(Master_cs[2]), .MISO(Slave_3_miso));
  Slave_reg Slave_2 (.SCLK(Master_sclk), .MOSI(Master_mosi), .Enable(Master_cs[1]), .MISO(Slave_2_miso));
  Slave_reg Slave_1 (.SCLK(Master_sclk), .MOSI(Master_mosi), .Enable(Master_cs[0]), .MISO(Slave_1_miso));
endmodule

module Master_reg (
  input  MISO,
  input  Enable,
  input  [1:0] Slave_select,
  output SCLK,
  output MOSI,
  output [2:0] CS
);

  wire d_ff_1_q, d_ff_2_q, d_ff_3_q, d_ff_4_q, d_ff_5_q, d_ff_6_q, d_ff_7_q;

  Clock CLK (.out(SCLK));
  D_Flip_Flop d_ff_1 (.clk(SCLK), .D(MISO), .Q(d_ff_1_q), .preset(1'b0), .en(Enable), .reset(1'b0));  // open: Qn
  D_Flip_Flop d_ff_2 (.clk(SCLK), .D(d_ff_1_q), .Q(d_ff_2_q), .preset(1'b0), .en(Enable), .reset(1'b0));  // open: Qn
  D_Flip_Flop d_ff_3 (.clk(SCLK), .D(d_ff_2_q), .Q(d_ff_3_q), .preset(1'b0), .en(Enable), .reset(1'b0));  // open: Qn
  not not_1 (CS[2], Slave_select[1]);
  not not_2 (CS[1], Slave_select[0]);
  or or_1 (CS[0], Slave_select[1], Slave_select[0]);
  D_Flip_Flop d_ff_4 (.clk(SCLK), .D(d_ff_3_q), .Q(d_ff_4_q), .preset(1'b0), .en(Enable), .reset(1'b0));  // open: Qn
  D_Flip_Flop d_ff_5 (.clk(SCLK), .D(d_ff_4_q), .Q(d_ff_5_q), .preset(1'b0), .en(Enable), .reset(1'b0));  // open: Qn
  D_Flip_Flop d_ff_6 (.clk(SCLK), .D(d_ff_5_q), .Q(d_ff_6_q), .preset(1'b0), .en(Enable), .reset(1'b0));  // open: Qn
  D_Flip_Flop d_ff_7 (.clk(SCLK), .D(d_ff_6_q), .Q(d_ff_7_q), .preset(1'b0), .en(Enable), .reset(1'b0));  // open: Qn
  D_Flip_Flop d_ff_8 (.clk(SCLK), .D(d_ff_7_q), .Q(MOSI), .preset(1'b0), .en(Enable), .reset(1'b0));  // open: Qn
endmodule

module Slave_reg (
  input  SCLK,
  input  MOSI,
  input  Enable,
  output MISO
);

  wire d_ff_1_q, d_ff_2_q, d_ff_3_q, d_ff_4_q, d_ff_5_q, d_ff_6_q, d_ff_7_q, not_1_out;

  not not_1 (not_1_out, Enable);
  D_Flip_Flop d_ff_1 (.clk(SCLK), .D(MOSI), .Q(d_ff_1_q), .preset(1'b0), .en(not_1_out), .reset(1'b0));  // open: Qn
  D_Flip_Flop d_ff_2 (.clk(SCLK), .D(d_ff_1_q), .Q(d_ff_2_q), .preset(1'b0), .en(not_1_out), .reset(1'b0));  // open: Qn
  D_Flip_Flop d_ff_3 (.clk(SCLK), .D(d_ff_2_q), .Q(d_ff_3_q), .preset(1'b0), .en(not_1_out), .reset(1'b0));  // open: Qn
  D_Flip_Flop d_ff_4 (.clk(SCLK), .D(d_ff_3_q), .Q(d_ff_4_q), .preset(1'b0), .en(not_1_out), .reset(1'b0));  // open: Qn
  D_Flip_Flop d_ff_5 (.clk(SCLK), .D(d_ff_4_q), .Q(d_ff_5_q), .preset(1'b0), .en(not_1_out), .reset(1'b0));  // open: Qn
  D_Flip_Flop d_ff_6 (.clk(SCLK), .D(d_ff_5_q), .Q(d_ff_6_q), .preset(1'b0), .en(not_1_out), .reset(1'b0));  // open: Qn
  D_Flip_Flop d_ff_7 (.clk(SCLK), .D(d_ff_6_q), .Q(d_ff_7_q), .preset(1'b0), .en(not_1_out), .reset(1'b0));  // open: Qn
  D_Flip_Flop d_ff_8 (.clk(SCLK), .D(d_ff_7_q), .Q(MISO), .preset(1'b0), .en(not_1_out), .reset(1'b0));  // open: Qn
endmodule
